# Fritzing sketch pov (saved by Fritzing 0.9.1b)
breadboards: 1

parts:
  U15 = 74HC595 [package="DIP16 [THT]"]
  U16 = 74HC595 [package="DIP16 [THT]"]
  U17 = 74HC595 [package="DIP16 [THT]"]
  U18 = 74HC595 [package="DIP16 [THT]"]
  R126 = Resistor [tolerance=±5% resistance=10k package=THT]
  Componente1 = Arduino Mega 2560 (Rev3)
  Q1 = LTR-301 [package=ltr-301]
  D1 = LTE-302 [package=lte-302]
  R166 = Resistor [tolerance=±5% resistance=330 package=THT]
  R167 = Resistor [tolerance=±5% resistance=2M package=THT]
  J1 = female pin header, 5 pins [form="♀ (female)"]
  J2 = double row female pin header, 28 pins [form="♀ (female)"]
  J3 = double row female pin header, 32 pins [form="♀ (female)"]

nets:
  N1: U15.Q1, J3.pin26
  N2: U15.Q2, J3.pin27
  N3: U15.Q3, J3.pin28
  N4: U15.Q4, J3.pin29
  N5: U15.Q5, J3.pin30
  N6: U15.Q6, J3.pin31
  N7: U15.Q7, J3.pin32
  GND: U15.GND, U16.GND, U17.GND, U18.GND, Componente1.GND, D1.C, R167.Pin_1, J1.pin5
  5V: U15.MR, U15.VCC, U16.MR, U16.VCC, U17.MR, U17.VCC, U18.MR, U18.VCC, Componente1.5V, Q1.C, R166.Pin_0, J1.pin1
  N8: U15.SH_CP, U16.SH_CP, U17.SH_CP, U18.SH_CP, Componente1.D9_PWM, J1.pin2
  N9: U15.ST_CP, U16.ST_CP, U17.ST_CP, U18.ST_CP, R126.Pin_0, Componente1.D7_PWM, J1.pin4
  N10: U15.OE, U16.OE, U17.OE, U18.OE, R126.Pin_1
  N11: U15.DS, U16.Q7'
  N12: U15.Q0, J3.pin25
  N13: U16.Q1, J3.pin17
  N14: U16.Q2, J3.pin18
  N15: U16.Q3, J3.pin19
  N16: U16.Q4, J3.pin20
  N17: U16.Q5, J3.pin21
  N18: U16.Q6, J3.pin22
  N19: U16.Q7, J3.pin23
  N20: U16.DS, U17.Q7'
  N21: U16.Q0, J3.pin24
  N22: U17.Q1, J3.pin10
  N23: U17.Q2, J3.pin11
  N24: U17.Q3, J3.pin12
  N25: U17.Q4, J3.pin13
  N26: U17.Q5, J3.pin14
  N27: U17.Q6, J3.pin15
  N28: U17.Q7, J3.pin16
  N29: U17.DS, U18.Q7'
  N30: U17.Q0, J3.pin9
  N31: U18.Q1, J3.pin2
  N32: U18.Q2, J3.pin3
  N33: U18.Q3, J3.pin4
  N34: U18.Q4, J3.pin5
  N35: U18.Q5, J3.pin6
  N36: U18.Q6, J3.pin7
  N37: U18.Q7, J3.pin8
  N38: U18.DS, Componente1.D8_PWM, J1.pin3
  N39: U18.Q0, J3.pin1
  N40: Componente1.D22, J2.pin1
  N41: Componente1.D23, J2.pin2
  N42: Componente1.D24, J2.pin3
  N43: Componente1.D25, J2.pin4
  N44: Componente1.D26, J2.pin5
  N45: Componente1.D27, J2.pin6
  N46: Componente1.D28, J2.pin7
  N47: Componente1.D29, J2.pin8
  N48: Componente1.D30, J2.pin9
  N49: Componente1.D31, J2.pin10
  N50: Componente1.D32, J2.pin11
  N51: Componente1.D33, J2.pin12
  N52: Componente1.D34, J2.pin13
  N53: Componente1.D35, J2.pin14
  N54: Componente1.D36, J2.pin15
  N55: Componente1.D37, J2.pin16
  N56: Componente1.D38, J2.pin27
  N57: Componente1.D39, J2.pin26
  N58: Componente1.D40, J2.pin25
  N59: Componente1.D41, J2.pin24
  N60: Componente1.D42, J2.pin23
  N61: Componente1.D43, J2.pin22
  N62: Componente1.D44, J2.pin21
  N63: Componente1.D45, J2.pin20
  N64: Componente1.D46, J2.pin19
  N65: Componente1.D47, J2.pin18
  N66: Componente1.D48, J2.pin17
  N67: Componente1.D49, Q1.E, R167.Pin_0, J2.pin28
  N68: D1.A, R166.Pin_1
