# Fritzing sketch pov 2 circuit (saved by Fritzing 0.9.1b)
breadboards: 1

parts:
  Componente1 = Arduino Nano (Rev3.0)
  Componente2 = Real Time Clock Module - DS1307 RTC Breakout Board
  BAT1 = BC9VPC [package=bc9vpc]
  LED1 = LED - 5mm [color="Red (633nm)" package="5 mm [THT]"]
  R1 = Resistor [tolerance=±5% resistance=330 package=THT]
  LED2 = LED - 5mm [color="Red (633nm)" package="5 mm [THT]"]
  R2 = Resistor [tolerance=±5% resistance=330 package=THT]
  LED3 = LED - 5mm [color="Red (633nm)" package="5 mm [THT]"]
  R3 = Resistor [tolerance=±5% resistance=330 package=THT]
  LED4 = LED - 5mm [color="Red (633nm)" package="5 mm [THT]"]
  R4 = Resistor [tolerance=±5% resistance=330 package=THT]
  LED5 = LED - 5mm [color="Red (633nm)" package="5 mm [THT]"]
  R5 = Resistor [tolerance=±5% resistance=330 package=THT]
  LED6 = LED - 5mm [color="Red (633nm)" package="5 mm [THT]"]
  LED7 = LED - 5mm [color="Red (633nm)" package="5 mm [THT]"]
  LED8 = LED - 5mm [color="Red (633nm)" package="5 mm [THT]"]
  LED9 = LED - 5mm [color="Red (633nm)" package="5 mm [THT]"]
  LED10 = LED - 5mm [color="Red (633nm)" package="5 mm [THT]"]
  R6 = Resistor [tolerance=±5% resistance=330 package=THT]
  R7 = Resistor [tolerance=±5% resistance=330 package=THT]
  R8 = Resistor [tolerance=±5% resistance=330 package=THT]
  R9 = Resistor [tolerance=±5% resistance=330 package=THT]
  R10 = Resistor [tolerance=±5% resistance=330 package=THT]
  HD_alimentaçao_externa = Stepper Motor - Bipolar

nets:
  GND: Componente1.GND, Componente2.GND, BAT1.V-, LED1.cathode, LED2.cathode, LED3.cathode, LED4.cathode, LED5.cathode, LED6.cathode, LED7.cathode, LED8.cathode, LED9.cathode, LED10.cathode
  N1: Componente1.D3, R10.Pin_1
  N2: Componente1.D4, R7.Pin_1
  N3: Componente1.D5, R9.Pin_1
  N4: Componente1.D6, R8.Pin_1
  N5: Componente1.D7, R6.Pin_1
  N6: Componente1.D8, R5.Pin_1
  N7: Componente1.D9, R4.Pin_1
  N8: Componente1.D10, R3.Pin_1
  N9: Componente1.D11/MOSI, R2.Pin_1
  N10: Componente1.D12/MISO, R1.Pin_1
  5V: Componente1.5V, Componente2.5V, BAT1.V+
  N11: Componente1.A5, Componente2.SCL
  N12: Componente1.A4, Componente2.SDA
  N13: LED1.anode, R1.Pin_0
  N14: LED2.anode, R2.Pin_0
  N15: LED3.anode, R3.Pin_0
  N16: LED4.anode, R4.Pin_0
  N17: LED5.anode, R5.Pin_0
  N18: LED6.anode, R6.Pin_0
  N19: LED7.anode, R9.Pin_0
  N20: LED8.anode, R7.Pin_0
  N21: LED9.anode, R10.Pin_0
  N22: LED10.anode, R8.Pin_0
  N23: HD_alimentaçao_externa.A, HD_alimentaçao_externa.C, HD_alimentaçao_externa.B, HD_alimentaçao_externa.D
